# Fritzing sketch Sketch (saved by Fritzing 1.0.0d)

parts:
  A1 = Esp32-c3 super mini
  HC-SR04_Sensor_1 = HC-SR04 Ultrasonic Distance Sensor

nets:
  N1: A1.Pin_7, HC-SR04_Sensor_1.ECHO
  N2: A1.Pin_8, HC-SR04_Sensor_1.TRIG
  N3: A1.Pin_14, HC-SR04_Sensor_1.VCC
  N4: A1.Pin_15, HC-SR04_Sensor_1.GND

custom parts:
  Esp32-c3 super mini: ESP32-C3 Development Board ESP32 SuperMini Development Board ESP32 Development Board WiFi Bluetooth.
