# Fritzing sketch Sketch (saved by Fritzing 1.0.6)

parts:
  M1 = STM32F103C8T6 blue mini board
  RE1 = KY-040 Rotary encoder [package="Breakout board"]
  R1 = Resistor [tolerance=±5% power=0.25W resistance=330 package=THT]
  LED1 = LED - 5mm [color="Yellow (592nm)" current=0.030A package="5 mm [THT]"]

nets:
  N1: M1.A8, R1.Pin_1
  N2: M1.B7, RE1.CLK
  N3: M1.B8, RE1.DT
  N4: M1.B9, RE1.SW
  GND: M1.G, M1.GND, RE1.GND, LED1.cathode
  3.3V: M1.3.3V, RE1.Vcc

custom parts:
  KY-040 Rotary encoder: KY-040 Rotary Encoder with switch on breakout borad from AZ Delivery
