# Fritzing sketch Sketch (saved by Fritzing 1.0.0d)

parts:
  A1 = Esp32-c3 super mini
  Part1 = Adafruit VL530X Time of Flight Distance Sensor [part_number="Adafruit #3317"]

nets:
  N1: A1.Pin_10, Part1.GPIO
  N2: A1.Pin_11, Part1.SDA
  N3: A1.Pin_12, Part1.SCL
  N4: A1.Pin_14, Part1.VCC
  N5: A1.Pin_15, Part1.GND

custom parts:
  Esp32-c3 super mini: ESP32-C3 Development Board ESP32 SuperMini Development Board ESP32 Development Board WiFi Bluetooth.
  Adafruit VL530X Time of Flight Distance Sensor: The VL53L0X is a Time of Flight distance sensor like no other you've used! The sensor contains a very tiny invisible laser source, and a matching sensor. The VL53L0X can detect the "time of flight", or how long the light has taken to bounce back to the sensor. Since it uses a very narrow light source, it is good for determining distance of only the surface directly in front of it. Unlike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
