# Fritzing sketch Sketch (saved by Fritzing 1.0.0d)
breadboards: 1

parts:
  A1 = Esp32-c3 super mini
  LED1 = LED - 3mm [color="Infrared (940nm)" current=30mA package="3 mm [THT]"]
  R1 = Resistor [tolerance=±5% power=0.25W resistance=220 package=THT]
  R2 = Resistor [tolerance=±5% power=0.25W resistance=10k package=THT]
  R3 = Photocell (LDR) [package=THT]

nets:
  N1: A1.Pin_1, R2.Pin_0, R3.pin_0
  N2: A1.Pin_14, LED1.anode, R1.Pin_1, R3.pin_1
  N3: A1.Pin_15, R2.Pin_1
  N4: LED1.cathode, R1.Pin_0

notes:
  940nm IR Receiver. Hold it above the emitter so that the emitter and receiver are directly pointing towards each other.

custom parts:
  Esp32-c3 super mini: ESP32-C3 Development Board ESP32 SuperMini Development Board ESP32 Development Board WiFi Bluetooth.
