# Fritzing sketch Sketch (saved by Fritzing 1.0.2b)
breadboards: 1

parts:
  R1 = Resistor [tolerance=±5% power=0.25W resistance=220 package=THT]
  LED1 = LED - 5mm [color="Infrared (940nm)" current=0.030A package="5 mm [THT]"]
  A1 = Esp32-c3 super mini

nets:
  N1: R1.Pin_0, A1.Pin_16
  N2: R1.Pin_1, LED1.cathode
  N3: LED1.anode, A1.Pin_9

custom parts:
  Esp32-c3 super mini: ESP32-C3 Development Board ESP32 SuperMini Development Board ESP32 Development Board WiFi Bluetooth.
