# Fritzing sketch Sketch (saved by Fritzing 1.0.4)

parts:
  A1 = Esp32-c3 super mini
  A2 = Micro SD card reader

nets:
  N1: A1.Pin_1, A2.Pin_5
  N2: A1.Pin_2, A2.Pin_3
  N3: A1.Pin_9, A2.Pin_2
  N4: A1.Pin_13, A2.Pin_4
  N5: A1.Pin_14, A2.Pin_1
  N6: A1.Pin_15, A2.Pin_6

custom parts:
  Esp32-c3 super mini: ESP32-C3 Development Board ESP32 SuperMini Development Board ESP32 Development Board WiFi Bluetooth.
  Micro SD card reader: Micro SD card reader.
