# Fritzing sketch Sketch (saved by Fritzing 1.0.4)

parts:
  A1 = Esp32-c3 super mini
  Part1 = RFID-RC522-v3

nets:
  N1: A1.Pin_1, Part1.MISO
  N2: A1.Pin_2, Part1.MOSI
  N3: A1.Pin_6, Part1.RST
  N4: A1.Pin_8, Part1.SDA
  N5: A1.Pin_11, Part1.IRQ
  N6: A1.Pin_13, Part1.SCK
  N7: A1.Pin_14, Part1.3.3V
  N8: A1.Pin_15, Part1.GND

custom parts:
  Esp32-c3 super mini: ESP32-C3 Development Board ESP32 SuperMini Development Board ESP32 Development Board WiFi Bluetooth.
  RFID-RC522-v3: A simple China made RFID-RC522 Reader (6x4 cm); do check the pin labels, as this is a MFRC522 based clone.
