# Fritzing sketch Sketch (saved by Fritzing 1.0.2b)
breadboards: 1

parts:
  U1 = Sharp PC817 [package=THT]
  U2 = Sharp PC817 [package=THT]
  U3 = Sharp PC817 [package=THT]
  U4 = Sharp PC817 [package=THT]
  U5 = Sharp PC817 [package=THT]
  U6 = Sharp PC817 [package=THT]
  R1 = Resistor [tolerance=±5% resistance=220 package="0603 [SMD]"]
  R2 = Resistor [tolerance=±5% resistance=220 package="0603 [SMD]"]
  A1 = Esp32-c3 super mini
  R3 = Resistor [tolerance=±5% resistance=220 package="1206 [SMD]"]
  R4 = Resistor [tolerance=±5% resistance=220 package="1206 [SMD]"]

nets:
  N1: U1.Pin_1, U2.Pin_1, R1.Pin_1, R2.Pin_1
  N2: U1.Pin_2, U2.Pin_2, U3.Pin_2, U4.Pin_2, A1.Pin_15
  N3: U1.Pin_4, U2.Pin_3
  N4: U1.Pin_3, U2.Pin_4
  N5: U3.Pin_1, U4.Pin_1
  N6: U3.Pin_4, U4.Pin_3
  N7: U3.Pin_3, U4.Pin_4
  N8: U5.Pin_2, R3.Pin_0
  N9: U5.Pin_4, U6.Pin_4, A1.Pin_16
  N10: U5.Pin_3, R1.Pin_0, A1.Pin_6
  N11: U6.Pin_2, R4.Pin_0
  N12: U6.Pin_3, R2.Pin_0, A1.Pin_5

notes:
  Power Button
  Reset Button
  Power LED +
  Power LED -
  HDD LED +
  HDD LED -

custom parts:
  Esp32-c3 super mini: ESP32-C3 Development Board ESP32 SuperMini Development Board ESP32 Development Board WiFi Bluetooth.
